# Fritzing sketch Schema Beta (saved by Fritzing 0.9.10b)
breadboards: 2

parts:
  M3 = gear-motor
  M4 = gear-motor
  Componente2 = Adafruit Motor/Stepper/Servo Shield [part_number="Adafruit #1438"]
  LED1 = LED - 5mm [color="Red (633nm)" current=0.030 package="5 mm [THT]"]
  LED2 = LED - 5mm [color="Red (633nm)" current=0.030 package="5 mm [THT]"]
  R1 = Resistor [tolerance=±5% power=0.25 resistance=220 package=THT]
  R2 = Resistor [tolerance=±5% power=0.25 resistance=220 package=THT]
  HC-SR04_Sensor_1 = HC-SR04 Ultrasonic Distance Sensor
  Componente3 = Bluetooth HC-05 Macho

nets:
  N1: M3.pin_1, Componente2.M4A
  N2: M3.pin_2, Componente2.M4B
  N3: M4.pin_1, Componente2.M2A
  N4: M4.pin_2, Componente2.M2B
  N5: Componente2.AD1, R1.Pin_1
  N6: Componente2.AD0, R2.Pin_1
  N7: Componente2.D5, HC-SR04_Sensor_1.ECHO
  GND: Componente2.GND, LED1.cathode, LED2.cathode, HC-SR04_Sensor_1.GND, Componente3.GND
  VCC: Componente2.+5V, HC-SR04_Sensor_1.VCC, Componente3.VCC
  N8: Componente2.D2, Componente3.TXD
  N9: Componente2.D3, Componente3.RXD
  N10: Componente2.D4, HC-SR04_Sensor_1.TRIG
  N11: LED1.anode, R2.Pin_0
  N12: LED2.anode, R1.Pin_0

custom parts:
  Adafruit Motor/Stepper/Servo Shield: The original Adafruit Motorshield kit is one of our most beloved kits, which is why we decided to make something even better. We have upgraded the shield kit to make the bestest, easiest way to drive DC and Stepper motors. This shield will make quick work of your next robotics project! We kept the ability to drive up to 4 DC motors or 2 stepper motors, but added many improvements: Instead of a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
